# Fritzing sketch 28BYJ-48-driver_and_motor-1 (saved by Fritzing 0.9.6b)

parts:
  Driver1 = 28BYJ-48 Driver Module [part_number=ULN2003 package=THT]
  Power_plug1 = Power plug
  MCU1 = Raspberry Pi Zero
  Driver2 = 28BYJ-48 Driver Module [part_number=ULN2003 package=THT]
  SM2 = 28BYJ-48 Stepper Motor [part_number=28BYJ-48]
  Power_plug2 = Power plug
  SM1 = 28BYJ-48 Stepper Motor [part_number=28BYJ-48]

nets:
  N1: Driver1.IN1, MCU1.pin_11
  N2: Driver1.IN2, MCU1.pin_12
  N3: Driver1.IN3, MCU1.pin_13
  N4: Driver1.IN4, MCU1.pin_15
  GND: Driver1.GND, Power_plug1.GND
  N5: Driver1.Vmotor, Power_plug1.VCC
  N6: Driver1.blue-pin, SM1.blue-pin
  N7: Driver1.pink-pin, SM1.pink-pin
  N8: Driver1.yellow-pin, SM1.yellow-pin
  N9: Driver1.orange-pin, SM1.orange-pin
  N10: Driver1.red-pin, SM1.red-pin
  N11: MCU1.pin_6, MCU1.pin_39, Driver2.IN1
  N12: MCU1.pin_33, Driver2.IN4
  N13: MCU1.pin_35, Driver2.IN3
  N14: MCU1.pin_37, Driver2.IN2
  GND_2: Driver2.GND, Power_plug2.GND
  N15: Driver2.Vmotor, Power_plug2.VCC
  N16: Driver2.blue-pin, SM2.blue-pin
  N17: Driver2.pink-pin, SM2.pink-pin
  N18: Driver2.yellow-pin, SM2.yellow-pin
  N19: Driver2.orange-pin, SM2.orange-pin
  N20: Driver2.red-pin, SM2.red-pin

custom parts:
  28BYJ-48 Driver Module: ULN2003 Driver Module for the 28BYJ-48 Unipolar Stepper Motor LED A - Blue wire - Bottom coil left LED B - Pink wire - Top coil left LED C - Yellow wire - Bottom coil right LED D - Orange wire - Top coil right Common rail - red Connector pins: blue - pink - yellow - orange - red Control pins - IN1 to IN4 Power pins - GND & Vmotor (5-12V) On/Off jumper (if removed, power to motor is cut).
  28BYJ-48 Stepper Motor: Unipolar Stepper Motor 28BYJ-48 Top coil - pink & orange Bottom coil - blue & yellow Common rail - red Connector pins: blue - pink - yellow - orange - red
