# Fritzing sketch LED (saved by Fritzing 0.9.6b)
breadboards: 1

parts:
  MCU1 = Raspberry Pi Zero
  Q1 = NPN-Transistor [package="TO92 [THT]"]
  LED1 = LEDs [package=fkit-led-1206]
  R2 = Resistor [tolerance=±5% power=0.25 resistance=220 package=THT]
  R1 = Resistor [tolerance=±5% power=0.25 resistance=10 package=THT]

nets:
  N1: MCU1.pin_2, MCU1.pin_4, LED1.A
  N2: MCU1.pin_6, MCU1.pin_14, MCU1.pin_39, Q1.E
  N3: MCU1.pin_10, R2.Pin_0
  N4: Q1.B, R2.Pin_1
  N5: Q1.C, R1.Pin_0
  N6: LED1.C, R1.Pin_1
